// Logisim project skeleton.circ as structural Verilog: 3 circuits, main circuit main
// bresenham-logisim - Implementation of Bresenham's line algorithm using logisim
// Copyright (C) 2019 lxylxy123456
// This program is free software: you can redistribute it and/or modify
// it under the terms of the GNU Affero General Public License as
// published by the Free Software Foundation, either version 3 of the
// License, or (at your option) any later version.
// This program is distributed in the hope that it will be useful,
// but WITHOUT ANY WARRANTY; without even the implied warranty of
// MERCHANTABILITY or FITNESS FOR A PARTICULAR PURPOSE. See the
// GNU Affero General Public License for more details.
// You should have received a copy of the GNU Affero General Public License
// along with this program. If not, see <https://www.gnu.org/licenses/>.
module main (
  input  [4:0] row,
  input  [4:0] col,
  input  write,
  input  clear
);

  wire clock_1_out, enumerator_1_write;
  wire [4:0] enumerator_1_col, enumerator_1_row;
  wire [31:0] editor_1_out_6, editor_1_out_7, editor_1_out_8, editor_1_out_9, editor_1_out_10,
       editor_1_out_11, editor_1_out_12, editor_1_out_13, editor_1_out_14, editor_1_out_15, editor_1_out_16,
       editor_1_out_17, editor_1_out_18, editor_1_out_19, editor_1_out_20, editor_1_out_21, editor_1_out_22,
       editor_1_out_23, editor_1_out_24, editor_1_out_25, editor_1_out_26, editor_1_out_27, editor_1_out_28,
       editor_1_out_29, editor_1_out_30, editor_1_out_31, editor_1_out_32, editor_1_out_33, editor_1_out_34,
       editor_1_out_35, editor_1_out_36, editor_1_out_37;

  enumerator enumerator_1 (
    .clock(clock_1_out), .row(enumerator_1_row), .col(enumerator_1_col), .write(enumerator_1_write));
  Clock clock_1 (.out(clock_1_out));
  DotMatrix #(.matrixcols(32), .matrixrows(32)) dotmatrix_1 (
    .col0(editor_1_out_6), .col1(editor_1_out_7), .col2(editor_1_out_8), .col3(editor_1_out_9),
    .col4(editor_1_out_10), .col5(editor_1_out_11), .col6(editor_1_out_12), .col7(editor_1_out_13),
    .col8(editor_1_out_14), .col9(editor_1_out_15), .col10(editor_1_out_16), .col11(editor_1_out_17),
    .col12(editor_1_out_18), .col13(editor_1_out_19), .col14(editor_1_out_20), .col15(editor_1_out_21),
    .col16(editor_1_out_22), .col17(editor_1_out_23), .col18(editor_1_out_24), .col19(editor_1_out_25),
    .col20(editor_1_out_26), .col21(editor_1_out_27), .col22(editor_1_out_28), .col23(editor_1_out_29),
    .col24(editor_1_out_30), .col25(editor_1_out_31), .col26(editor_1_out_32), .col27(editor_1_out_33),
    .col28(editor_1_out_34), .col29(editor_1_out_35), .col30(editor_1_out_36), .col31(editor_1_out_37));
  editor editor_1 (
    .row(enumerator_1_row), .col(enumerator_1_col), .write(enumerator_1_write), .clear(clear),
    .clock(clock_1_out), .out_6(editor_1_out_6), .out_7(editor_1_out_7), .out_8(editor_1_out_8),
    .out_9(editor_1_out_9), .out_10(editor_1_out_10), .out_11(editor_1_out_11), .out_12(editor_1_out_12),
    .out_13(editor_1_out_13), .out_14(editor_1_out_14), .out_15(editor_1_out_15), .out_16(editor_1_out_16),
    .out_17(editor_1_out_17), .out_18(editor_1_out_18), .out_19(editor_1_out_19), .out_20(editor_1_out_20),
    .out_21(editor_1_out_21), .out_22(editor_1_out_22), .out_23(editor_1_out_23), .out_24(editor_1_out_24),
    .out_25(editor_1_out_25), .out_26(editor_1_out_26), .out_27(editor_1_out_27), .out_28(editor_1_out_28),
    .out_29(editor_1_out_29), .out_30(editor_1_out_30), .out_31(editor_1_out_31), .out_32(editor_1_out_32),
    .out_33(editor_1_out_33), .out_34(editor_1_out_34), .out_35(editor_1_out_35), .out_36(editor_1_out_36),
    .out_37(editor_1_out_37));
endmodule

module editor (
  input  [4:0] row,
  input  [4:0] col,
  input  write,
  input  clear,
  input  clock,
  output [31:0] out_6,
  output [31:0] out_7,
  output [31:0] out_8,
  output [31:0] out_9,
  output [31:0] out_10,
  output [31:0] out_11,
  output [31:0] out_12,
  output [31:0] out_13,
  output [31:0] out_14,
  output [31:0] out_15,
  output [31:0] out_16,
  output [31:0] out_17,
  output [31:0] out_18,
  output [31:0] out_19,
  output [31:0] out_20,
  output [31:0] out_21,
  output [31:0] out_22,
  output [31:0] out_23,
  output [31:0] out_24,
  output [31:0] out_25,
  output [31:0] out_26,
  output [31:0] out_27,
  output [31:0] out_28,
  output [31:0] out_29,
  output [31:0] out_30,
  output [31:0] out_31,
  output [31:0] out_32,
  output [31:0] out_33,
  output [31:0] out_34,
  output [31:0] out_35,
  output [31:0] out_36,
  output [31:0] out_37
);

  wire comparator_1_eq, comparator_2_eq, comparator_3_eq, comparator_4_eq, comparator_5_eq, comparator_6_eq,
       comparator_7_eq, comparator_8_eq, comparator_9_eq, comparator_10_eq, comparator_11_eq,
       comparator_12_eq, comparator_13_eq, comparator_14_eq, comparator_15_eq, comparator_16_eq,
       comparator_17_eq, comparator_18_eq, comparator_19_eq, comparator_20_eq, comparator_21_eq,
       comparator_22_eq, comparator_23_eq, comparator_24_eq, comparator_25_eq, comparator_26_eq,
       comparator_27_eq, comparator_28_eq, comparator_29_eq, comparator_30_eq, comparator_31_eq,
       comparator_32_eq, or_1_out;
  wire [31:0] and_1_out, and_2_out, and_3_out, and_4_out, and_5_out, and_6_out, and_7_out, and_8_out,
       and_9_out, and_10_out, and_11_out, and_12_out, and_13_out, and_14_out, and_15_out, and_16_out,
       and_17_out, and_18_out, and_19_out, and_20_out, and_21_out, and_22_out, and_23_out, and_24_out,
       and_25_out, and_26_out, and_27_out, and_28_out, and_29_out, and_30_out, and_31_out, and_32_out,
       and_33_out, and_34_out, and_35_out, and_36_out, and_37_out, and_38_out, and_39_out, and_40_out,
       and_41_out, and_42_out, and_43_out, and_44_out, and_45_out, and_46_out, and_47_out, and_48_out,
       and_49_out, and_50_out, and_51_out, and_52_out, and_53_out, and_54_out, and_55_out, and_56_out,
       and_57_out, and_58_out, and_59_out, and_60_out, and_61_out, and_62_out, and_63_out, and_64_out,
       bit_extender_1_out, bit_extender_2_out, bit_extender_3_out, bit_extender_4_out, bit_extender_5_out,
       bit_extender_6_out, bit_extender_7_out, bit_extender_8_out, bit_extender_9_out, bit_extender_10_out,
       bit_extender_11_out, bit_extender_12_out, bit_extender_13_out, bit_extender_14_out,
       bit_extender_15_out, bit_extender_16_out, bit_extender_17_out, bit_extender_18_out,
       bit_extender_19_out, bit_extender_20_out, bit_extender_21_out, bit_extender_22_out,
       bit_extender_23_out, bit_extender_24_out, bit_extender_25_out, bit_extender_26_out,
       bit_extender_27_out, bit_extender_28_out, bit_extender_29_out, bit_extender_30_out,
       bit_extender_31_out, bit_extender_32_out, bit_extender_33_out, or_2_out, or_3_out, or_4_out, or_5_out,
       or_6_out, or_7_out, or_8_out, or_9_out, or_10_out, or_11_out, or_12_out, or_13_out, or_14_out,
       or_15_out, or_16_out, or_17_out, or_18_out, or_19_out, or_20_out, or_21_out, or_22_out, or_23_out,
       or_24_out, or_25_out, or_26_out, or_27_out, or_28_out, or_29_out, or_30_out, or_31_out, or_32_out,
       or_33_out, shifter_1_out;

  assign bit_extender_1_out = {{31{clear}}, clear};  // Bit_Extender bit_extender_1
  Shifter #(.width(32)) shifter_1 (.in(32'h1), .\dist (col), .out(shifter_1_out));
  or or_1 (or_1_out, write, clear);
  Comparator #(.width(5)) comparator_1 (.a({5{1'b0}}), .b(row), .eq(comparator_1_eq));  // open: gt, lt
  Comparator #(.width(5)) comparator_2 (.a(5'b00001), .b(row), .eq(comparator_2_eq));  // open: gt, lt
  Comparator #(.width(5)) comparator_3 (.a(5'b00010), .b(row), .eq(comparator_3_eq));  // open: gt, lt
  Comparator #(.width(5)) comparator_4 (.a(5'b00011), .b(row), .eq(comparator_4_eq));  // open: gt, lt
  Comparator #(.width(5)) comparator_5 (.a(5'b00100), .b(row), .eq(comparator_5_eq));  // open: gt, lt
  Comparator #(.width(5)) comparator_6 (.a(5'b00101), .b(row), .eq(comparator_6_eq));  // open: gt, lt
  Comparator #(.width(5)) comparator_7 (.a(5'b00110), .b(row), .eq(comparator_7_eq));  // open: gt, lt
  Comparator #(.width(5)) comparator_8 (.a(5'b00111), .b(row), .eq(comparator_8_eq));  // open: gt, lt
  Comparator #(.width(5)) comparator_9 (.a(5'b01000), .b(row), .eq(comparator_9_eq));  // open: gt, lt
  Comparator #(.width(5)) comparator_10 (.a(5'b01001), .b(row), .eq(comparator_10_eq));  // open: gt, lt
  Comparator #(.width(5)) comparator_11 (.a(5'b01010), .b(row), .eq(comparator_11_eq));  // open: gt, lt
  Comparator #(.width(5)) comparator_12 (.a(5'b01011), .b(row), .eq(comparator_12_eq));  // open: gt, lt
  Comparator #(.width(5)) comparator_13 (.a(5'b01100), .b(row), .eq(comparator_13_eq));  // open: gt, lt
  Comparator #(.width(5)) comparator_14 (.a(5'b01101), .b(row), .eq(comparator_14_eq));  // open: gt, lt
  Comparator #(.width(5)) comparator_15 (.a(5'b01110), .b(row), .eq(comparator_15_eq));  // open: gt, lt
  Comparator #(.width(5)) comparator_16 (.a(5'b01111), .b(row), .eq(comparator_16_eq));  // open: gt, lt
  Comparator #(.width(5)) comparator_17 (.a(5'b10000), .b(row), .eq(comparator_17_eq));  // open: gt, lt
  Comparator #(.width(5)) comparator_18 (.a(5'b10001), .b(row), .eq(comparator_18_eq));  // open: gt, lt
  Comparator #(.width(5)) comparator_19 (.a(5'b10010), .b(row), .eq(comparator_19_eq));  // open: gt, lt
  Comparator #(.width(5)) comparator_20 (.a(5'b10011), .b(row), .eq(comparator_20_eq));  // open: gt, lt
  Comparator #(.width(5)) comparator_21 (.a(5'b10100), .b(row), .eq(comparator_21_eq));  // open: gt, lt
  Comparator #(.width(5)) comparator_22 (.a(5'b10101), .b(row), .eq(comparator_22_eq));  // open: gt, lt
  Comparator #(.width(5)) comparator_23 (.a(5'b10110), .b(row), .eq(comparator_23_eq));  // open: gt, lt
  Comparator #(.width(5)) comparator_24 (.a(5'b10111), .b(row), .eq(comparator_24_eq));  // open: gt, lt
  Comparator #(.width(5)) comparator_25 (.a(5'b11000), .b(row), .eq(comparator_25_eq));  // open: gt, lt
  Comparator #(.width(5)) comparator_26 (.a(5'b11001), .b(row), .eq(comparator_26_eq));  // open: gt, lt
  Comparator #(.width(5)) comparator_27 (.a(5'b11010), .b(row), .eq(comparator_27_eq));  // open: gt, lt
  Comparator #(.width(5)) comparator_28 (.a(5'b11011), .b(row), .eq(comparator_28_eq));  // open: gt, lt
  Comparator #(.width(5)) comparator_29 (.a(5'b11100), .b(row), .eq(comparator_29_eq));  // open: gt, lt
  Comparator #(.width(5)) comparator_30 (.a(5'b11101), .b(row), .eq(comparator_30_eq));  // open: gt, lt
  Comparator #(.width(5)) comparator_31 (.a(5'b11110), .b(row), .eq(comparator_31_eq));  // open: gt, lt
  Comparator #(.width(5)) comparator_32 (.a({5{1'b1}}), .b(row), .eq(comparator_32_eq));  // open: gt, lt
  assign bit_extender_2_out = {{31{comparator_1_eq}}, comparator_1_eq};  // Bit_Extender bit_extender_2
  assign and_1_out = bit_extender_2_out & shifter_1_out;  // AND_Gate and_1, 32 bits wide
  assign bit_extender_3_out = {{31{comparator_2_eq}}, comparator_2_eq};  // Bit_Extender bit_extender_3
  assign and_2_out = bit_extender_3_out & shifter_1_out;  // AND_Gate and_2, 32 bits wide
  assign bit_extender_4_out = {{31{comparator_3_eq}}, comparator_3_eq};  // Bit_Extender bit_extender_4
  assign and_3_out = bit_extender_4_out & shifter_1_out;  // AND_Gate and_3, 32 bits wide
  assign bit_extender_5_out = {{31{comparator_4_eq}}, comparator_4_eq};  // Bit_Extender bit_extender_5
  assign and_4_out = bit_extender_5_out & shifter_1_out;  // AND_Gate and_4, 32 bits wide
  assign bit_extender_6_out = {{31{comparator_5_eq}}, comparator_5_eq};  // Bit_Extender bit_extender_6
  assign and_5_out = bit_extender_6_out & shifter_1_out;  // AND_Gate and_5, 32 bits wide
  assign bit_extender_7_out = {{31{comparator_6_eq}}, comparator_6_eq};  // Bit_Extender bit_extender_7
  assign and_6_out = bit_extender_7_out & shifter_1_out;  // AND_Gate and_6, 32 bits wide
  assign bit_extender_8_out = {{31{comparator_7_eq}}, comparator_7_eq};  // Bit_Extender bit_extender_8
  assign and_7_out = bit_extender_8_out & shifter_1_out;  // AND_Gate and_7, 32 bits wide
  assign bit_extender_9_out = {{31{comparator_8_eq}}, comparator_8_eq};  // Bit_Extender bit_extender_9
  assign and_8_out = bit_extender_9_out & shifter_1_out;  // AND_Gate and_8, 32 bits wide
  assign bit_extender_10_out = {{31{comparator_9_eq}}, comparator_9_eq};  // Bit_Extender bit_extender_10
  assign and_9_out = bit_extender_10_out & shifter_1_out;  // AND_Gate and_9, 32 bits wide
  assign bit_extender_11_out = {{31{comparator_10_eq}}, comparator_10_eq};  // Bit_Extender bit_extender_11
  assign and_10_out = bit_extender_11_out & shifter_1_out;  // AND_Gate and_10, 32 bits wide
  assign bit_extender_12_out = {{31{comparator_11_eq}}, comparator_11_eq};  // Bit_Extender bit_extender_12
  assign and_11_out = bit_extender_12_out & shifter_1_out;  // AND_Gate and_11, 32 bits wide
  assign bit_extender_13_out = {{31{comparator_12_eq}}, comparator_12_eq};  // Bit_Extender bit_extender_13
  assign and_12_out = bit_extender_13_out & shifter_1_out;  // AND_Gate and_12, 32 bits wide
  assign bit_extender_14_out = {{31{comparator_13_eq}}, comparator_13_eq};  // Bit_Extender bit_extender_14
  assign and_13_out = bit_extender_14_out & shifter_1_out;  // AND_Gate and_13, 32 bits wide
  assign bit_extender_15_out = {{31{comparator_14_eq}}, comparator_14_eq};  // Bit_Extender bit_extender_15
  assign and_14_out = bit_extender_15_out & shifter_1_out;  // AND_Gate and_14, 32 bits wide
  assign bit_extender_16_out = {{31{comparator_15_eq}}, comparator_15_eq};  // Bit_Extender bit_extender_16
  assign and_15_out = bit_extender_16_out & shifter_1_out;  // AND_Gate and_15, 32 bits wide
  assign bit_extender_17_out = {{31{comparator_16_eq}}, comparator_16_eq};  // Bit_Extender bit_extender_17
  assign and_16_out = bit_extender_17_out & shifter_1_out;  // AND_Gate and_16, 32 bits wide
  assign bit_extender_18_out = {{31{comparator_17_eq}}, comparator_17_eq};  // Bit_Extender bit_extender_18
  assign and_17_out = bit_extender_18_out & shifter_1_out;  // AND_Gate and_17, 32 bits wide
  assign bit_extender_19_out = {{31{comparator_18_eq}}, comparator_18_eq};  // Bit_Extender bit_extender_19
  assign and_18_out = bit_extender_19_out & shifter_1_out;  // AND_Gate and_18, 32 bits wide
  assign bit_extender_20_out = {{31{comparator_19_eq}}, comparator_19_eq};  // Bit_Extender bit_extender_20
  assign and_19_out = bit_extender_20_out & shifter_1_out;  // AND_Gate and_19, 32 bits wide
  assign bit_extender_21_out = {{31{comparator_20_eq}}, comparator_20_eq};  // Bit_Extender bit_extender_21
  assign and_20_out = bit_extender_21_out & shifter_1_out;  // AND_Gate and_20, 32 bits wide
  assign bit_extender_22_out = {{31{comparator_21_eq}}, comparator_21_eq};  // Bit_Extender bit_extender_22
  assign and_21_out = bit_extender_22_out & shifter_1_out;  // AND_Gate and_21, 32 bits wide
  assign bit_extender_23_out = {{31{comparator_22_eq}}, comparator_22_eq};  // Bit_Extender bit_extender_23
  assign and_22_out = bit_extender_23_out & shifter_1_out;  // AND_Gate and_22, 32 bits wide
  assign bit_extender_24_out = {{31{comparator_23_eq}}, comparator_23_eq};  // Bit_Extender bit_extender_24
  assign and_23_out = bit_extender_24_out & shifter_1_out;  // AND_Gate and_23, 32 bits wide
  assign bit_extender_25_out = {{31{comparator_24_eq}}, comparator_24_eq};  // Bit_Extender bit_extender_25
  assign and_24_out = bit_extender_25_out & shifter_1_out;  // AND_Gate and_24, 32 bits wide
  assign bit_extender_26_out = {{31{comparator_25_eq}}, comparator_25_eq};  // Bit_Extender bit_extender_26
  assign and_25_out = bit_extender_26_out & shifter_1_out;  // AND_Gate and_25, 32 bits wide
  assign bit_extender_27_out = {{31{comparator_26_eq}}, comparator_26_eq};  // Bit_Extender bit_extender_27
  assign and_26_out = bit_extender_27_out & shifter_1_out;  // AND_Gate and_26, 32 bits wide
  assign bit_extender_28_out = {{31{comparator_27_eq}}, comparator_27_eq};  // Bit_Extender bit_extender_28
  assign and_27_out = bit_extender_28_out & shifter_1_out;  // AND_Gate and_27, 32 bits wide
  assign bit_extender_29_out = {{31{comparator_28_eq}}, comparator_28_eq};  // Bit_Extender bit_extender_29
  assign and_28_out = bit_extender_29_out & shifter_1_out;  // AND_Gate and_28, 32 bits wide
  assign bit_extender_30_out = {{31{comparator_29_eq}}, comparator_29_eq};  // Bit_Extender bit_extender_30
  assign and_29_out = bit_extender_30_out & shifter_1_out;  // AND_Gate and_29, 32 bits wide
  assign bit_extender_31_out = {{31{comparator_30_eq}}, comparator_30_eq};  // Bit_Extender bit_extender_31
  assign and_30_out = bit_extender_31_out & shifter_1_out;  // AND_Gate and_30, 32 bits wide
  assign bit_extender_32_out = {{31{comparator_31_eq}}, comparator_31_eq};  // Bit_Extender bit_extender_32
  assign and_31_out = bit_extender_32_out & shifter_1_out;  // AND_Gate and_31, 32 bits wide
  assign bit_extender_33_out = {{31{comparator_32_eq}}, comparator_32_eq};  // Bit_Extender bit_extender_33
  assign and_32_out = bit_extender_33_out & shifter_1_out;  // AND_Gate and_32, 32 bits wide
  assign or_2_out = and_1_out | out_6;  // OR_Gate or_2, 32 bits wide
  assign and_33_out = or_2_out & ~bit_extender_1_out;  // AND_Gate and_33, 32 bits wide
  assign or_3_out = and_2_out | out_7;  // OR_Gate or_3, 32 bits wide
  assign and_34_out = or_3_out & ~bit_extender_1_out;  // AND_Gate and_34, 32 bits wide
  assign or_4_out = and_3_out | out_8;  // OR_Gate or_4, 32 bits wide
  assign and_35_out = or_4_out & ~bit_extender_1_out;  // AND_Gate and_35, 32 bits wide
  assign or_5_out = and_4_out | out_9;  // OR_Gate or_5, 32 bits wide
  assign and_36_out = or_5_out & ~bit_extender_1_out;  // AND_Gate and_36, 32 bits wide
  assign or_6_out = and_5_out | out_10;  // OR_Gate or_6, 32 bits wide
  assign and_37_out = or_6_out & ~bit_extender_1_out;  // AND_Gate and_37, 32 bits wide
  assign or_7_out = and_6_out | out_11;  // OR_Gate or_7, 32 bits wide
  assign and_38_out = or_7_out & ~bit_extender_1_out;  // AND_Gate and_38, 32 bits wide
  assign or_8_out = and_7_out | out_12;  // OR_Gate or_8, 32 bits wide
  assign and_39_out = or_8_out & ~bit_extender_1_out;  // AND_Gate and_39, 32 bits wide
  assign or_9_out = and_8_out | out_13;  // OR_Gate or_9, 32 bits wide
  assign and_40_out = or_9_out & ~bit_extender_1_out;  // AND_Gate and_40, 32 bits wide
  assign or_10_out = and_9_out | out_14;  // OR_Gate or_10, 32 bits wide
  assign and_41_out = or_10_out & ~bit_extender_1_out;  // AND_Gate and_41, 32 bits wide
  assign or_11_out = and_10_out | out_15;  // OR_Gate or_11, 32 bits wide
  assign and_42_out = or_11_out & ~bit_extender_1_out;  // AND_Gate and_42, 32 bits wide
  assign or_12_out = and_11_out | out_16;  // OR_Gate or_12, 32 bits wide
  assign and_43_out = or_12_out & ~bit_extender_1_out;  // AND_Gate and_43, 32 bits wide
  assign or_13_out = and_12_out | out_17;  // OR_Gate or_13, 32 bits wide
  assign and_44_out = or_13_out & ~bit_extender_1_out;  // AND_Gate and_44, 32 bits wide
  assign or_14_out = and_13_out | out_18;  // OR_Gate or_14, 32 bits wide
  assign and_45_out = or_14_out & ~bit_extender_1_out;  // AND_Gate and_45, 32 bits wide
  assign or_15_out = and_14_out | out_19;  // OR_Gate or_15, 32 bits wide
  assign and_46_out = or_15_out & ~bit_extender_1_out;  // AND_Gate and_46, 32 bits wide
  assign or_16_out = and_15_out | out_20;  // OR_Gate or_16, 32 bits wide
  assign and_47_out = or_16_out & ~bit_extender_1_out;  // AND_Gate and_47, 32 bits wide
  assign or_17_out = and_16_out | out_21;  // OR_Gate or_17, 32 bits wide
  assign and_48_out = or_17_out & ~bit_extender_1_out;  // AND_Gate and_48, 32 bits wide
  assign or_18_out = and_17_out | out_22;  // OR_Gate or_18, 32 bits wide
  assign and_49_out = or_18_out & ~bit_extender_1_out;  // AND_Gate and_49, 32 bits wide
  assign or_19_out = and_18_out | out_23;  // OR_Gate or_19, 32 bits wide
  assign and_50_out = or_19_out & ~bit_extender_1_out;  // AND_Gate and_50, 32 bits wide
  assign or_20_out = and_19_out | out_24;  // OR_Gate or_20, 32 bits wide
  assign and_51_out = or_20_out & ~bit_extender_1_out;  // AND_Gate and_51, 32 bits wide
  assign or_21_out = and_20_out | out_25;  // OR_Gate or_21, 32 bits wide
  assign and_52_out = or_21_out & ~bit_extender_1_out;  // AND_Gate and_52, 32 bits wide
  assign or_22_out = and_21_out | out_26;  // OR_Gate or_22, 32 bits wide
  assign and_53_out = or_22_out & ~bit_extender_1_out;  // AND_Gate and_53, 32 bits wide
  assign or_23_out = and_22_out | out_27;  // OR_Gate or_23, 32 bits wide
  assign and_54_out = or_23_out & ~bit_extender_1_out;  // AND_Gate and_54, 32 bits wide
  assign or_24_out = and_23_out | out_28;  // OR_Gate or_24, 32 bits wide
  assign and_55_out = or_24_out & ~bit_extender_1_out;  // AND_Gate and_55, 32 bits wide
  assign or_25_out = and_24_out | out_29;  // OR_Gate or_25, 32 bits wide
  assign and_56_out = or_25_out & ~bit_extender_1_out;  // AND_Gate and_56, 32 bits wide
  assign or_26_out = and_25_out | out_30;  // OR_Gate or_26, 32 bits wide
  assign and_57_out = or_26_out & ~bit_extender_1_out;  // AND_Gate and_57, 32 bits wide
  assign or_27_out = and_26_out | out_31;  // OR_Gate or_27, 32 bits wide
  assign and_58_out = or_27_out & ~bit_extender_1_out;  // AND_Gate and_58, 32 bits wide
  assign or_28_out = and_27_out | out_32;  // OR_Gate or_28, 32 bits wide
  assign and_59_out = or_28_out & ~bit_extender_1_out;  // AND_Gate and_59, 32 bits wide
  assign or_29_out = and_28_out | out_33;  // OR_Gate or_29, 32 bits wide
  assign and_60_out = or_29_out & ~bit_extender_1_out;  // AND_Gate and_60, 32 bits wide
  assign or_30_out = and_29_out | out_34;  // OR_Gate or_30, 32 bits wide
  assign and_61_out = or_30_out & ~bit_extender_1_out;  // AND_Gate and_61, 32 bits wide
  assign or_31_out = and_30_out | out_35;  // OR_Gate or_31, 32 bits wide
  assign and_62_out = or_31_out & ~bit_extender_1_out;  // AND_Gate and_62, 32 bits wide
  assign or_32_out = and_31_out | out_36;  // OR_Gate or_32, 32 bits wide
  assign and_63_out = or_32_out & ~bit_extender_1_out;  // AND_Gate and_63, 32 bits wide
  assign or_33_out = and_32_out | out_37;  // OR_Gate or_33, 32 bits wide
  assign and_64_out = or_33_out & ~bit_extender_1_out;  // AND_Gate and_64, 32 bits wide
  Register #(.width(32)) register_1 (.D(and_33_out), .en(or_1_out), .Q(out_6), .clk(clock));  // open: clr
  Register #(.width(32)) register_2 (.D(and_34_out), .en(or_1_out), .Q(out_7), .clk(clock));  // open: clr
  Register #(.width(32)) register_3 (.D(and_35_out), .en(or_1_out), .Q(out_8), .clk(clock));  // open: clr
  Register #(.width(32)) register_4 (.D(and_36_out), .en(or_1_out), .Q(out_9), .clk(clock));  // open: clr
  Register #(.width(32)) register_5 (.D(and_37_out), .en(or_1_out), .Q(out_10), .clk(clock));  // open: clr
  Register #(.width(32)) register_6 (.D(and_38_out), .en(or_1_out), .Q(out_11), .clk(clock));  // open: clr
  Register #(.width(32)) register_7 (.D(and_39_out), .en(or_1_out), .Q(out_12), .clk(clock));  // open: clr
  Register #(.width(32)) register_8 (.D(and_40_out), .en(or_1_out), .Q(out_13), .clk(clock));  // open: clr
  Register #(.width(32)) register_9 (.D(and_41_out), .en(or_1_out), .Q(out_14), .clk(clock));  // open: clr
  Register #(.width(32)) register_10 (.D(and_42_out), .en(or_1_out), .Q(out_15), .clk(clock));  // open: clr
  Register #(.width(32)) register_11 (.D(and_43_out), .en(or_1_out), .Q(out_16), .clk(clock));  // open: clr
  Register #(.width(32)) register_12 (.D(and_44_out), .en(or_1_out), .Q(out_17), .clk(clock));  // open: clr
  Register #(.width(32)) register_13 (.D(and_45_out), .en(or_1_out), .Q(out_18), .clk(clock));  // open: clr
  Register #(.width(32)) register_14 (.D(and_46_out), .en(or_1_out), .Q(out_19), .clk(clock));  // open: clr
  Register #(.width(32)) register_15 (.D(and_47_out), .en(or_1_out), .Q(out_20), .clk(clock));  // open: clr
  Register #(.width(32)) register_16 (.D(and_48_out), .en(or_1_out), .Q(out_21), .clk(clock));  // open: clr
  Register #(.width(32)) register_17 (.D(and_49_out), .en(or_1_out), .Q(out_22), .clk(clock));  // open: clr
  Register #(.width(32)) register_18 (.D(and_50_out), .en(or_1_out), .Q(out_23), .clk(clock));  // open: clr
  Register #(.width(32)) register_19 (.D(and_51_out), .en(or_1_out), .Q(out_24), .clk(clock));  // open: clr
  Register #(.width(32)) register_20 (.D(and_52_out), .en(or_1_out), .Q(out_25), .clk(clock));  // open: clr
  Register #(.width(32)) register_21 (.D(and_53_out), .en(or_1_out), .Q(out_26), .clk(clock));  // open: clr
  Register #(.width(32)) register_22 (.D(and_54_out), .en(or_1_out), .Q(out_27), .clk(clock));  // open: clr
  Register #(.width(32)) register_23 (.D(and_55_out), .en(or_1_out), .Q(out_28), .clk(clock));  // open: clr
  Register #(.width(32)) register_24 (.D(and_56_out), .en(or_1_out), .Q(out_29), .clk(clock));  // open: clr
  Register #(.width(32)) register_25 (.D(and_57_out), .en(or_1_out), .Q(out_30), .clk(clock));  // open: clr
  Register #(.width(32)) register_26 (.D(and_58_out), .en(or_1_out), .Q(out_31), .clk(clock));  // open: clr
  Register #(.width(32)) register_27 (.D(and_59_out), .en(or_1_out), .Q(out_32), .clk(clock));  // open: clr
  Register #(.width(32)) register_28 (.D(and_60_out), .en(or_1_out), .Q(out_33), .clk(clock));  // open: clr
  Register #(.width(32)) register_29 (.D(and_61_out), .en(or_1_out), .Q(out_34), .clk(clock));  // open: clr
  Register #(.width(32)) register_30 (.D(and_62_out), .en(or_1_out), .Q(out_35), .clk(clock));  // open: clr
  Register #(.width(32)) register_31 (.D(and_63_out), .en(or_1_out), .Q(out_36), .clk(clock));  // open: clr
  Register #(.width(32)) register_32 (.D(and_64_out), .en(or_1_out), .Q(out_37), .clk(clock));  // open: clr
endmodule

module enumerator (
  input  clock,
  output [4:0] row,
  output [4:0] col,
  output write
);

  wire adder_1_cout;
  wire [4:0] adder_1_out, adder_2_out, multiplexer_1_out;

  Register #(.width(5)) register_1 (.D(adder_1_out), .Q(row), .clk(clock));  // open: en, clr
  Register #(.width(5)) register_2 (.D(adder_2_out), .Q(col), .clk(clock));  // open: en, clr
  Adder #(.width(5)) adder_1 (.a(row), .b(5'b00001), .out(adder_1_out), .cout(adder_1_cout));  // open: cin
  Multiplexer #(.width(5), .enable("false")) multiplexer_1 (
    .in0({5{1'b0}}), .in1(5'b00001), .out(multiplexer_1_out), .sel(adder_1_cout));
  Adder #(.width(5)) adder_2 (.a(multiplexer_1_out), .b(col), .out(adder_2_out));  // open: cin, cout
  and and_1 (write, row[0], col[0]);
endmodule
